// Logisim project s-mips.circ as structural Verilog: 22 circuits, main circuit S-MIPS Board
module S_MIPS_Board (
  input  DESHABILITAR_DISPATCHER,
  output halt
);

  wire button_1_out, CLK, CS, d_ff_1_q, LCLR, LoadRAM, LoadRAMOn, LW, R_R_W, R_W, ram_dispatcher_1_finished,
       RCS, Reset_out, RST, TTY_EN;
  wire [2:0] KDB;
  wire [3:0] LMask, Mask, ram_1_read_time, ram_1_write_time, RMask;
  wire [6:0] KDB_DATA, TTY_DATA;
  wire [15:0] Addr, LAddr, RAddr;
  wire [31:0] I0, I1, I2, I3, LData, ram_1_data_out_0, ram_1_data_out_1, ram_1_data_out_2, ram_1_data_out_3,
       RI0, RI1, RI2, RI3;

  TTY #(.rows(25), .cols(80)) tty_1 (.data(TTY_DATA), .clk(CLK), .we(TTY_EN), .clr(RST));
  not not_1 (LoadRAMOn, ram_dispatcher_1_finished);
  RAM_Dispatcher ram_dispatcher_1 (
    .WriteTime(ram_1_write_time), .Clock(CLK), .Data(LData), .Address(LAddr), .Mask(LMask),
    .Finished(ram_dispatcher_1_finished), .Write(LW), .CLR(LCLR));
  Keyboard #(.buflen(64)) keyboard_1 (.clk(CLK), .re(KDB[0]), .avail(KDB[2]), .data(KDB_DATA));  // open: clr
  RAM ram_1 (
    .Address(RAddr), .Data_Out_0(ram_1_data_out_0), .Data_Out_1(ram_1_data_out_1),
    .Data_Out_2(ram_1_data_out_2), .Data_Out_3(ram_1_data_out_3), .Data_In_0(RI0), .Data_In_1(RI1),
    .Data_In_2(RI2), .Data_In_3(RI3), .Mask(RMask), .nRead_Write(R_R_W), .Chip_Select(RCS),
    .Read_Time(ram_1_read_time), .Reset(button_1_out), .Write_Time(ram_1_write_time));
  Button button_1 (.out(button_1_out));
  D_Flip_Flop d_ff_1 (.clk(CLK), .D(1'b1), .Q(d_ff_1_q), .reset(Reset_out));  // open: Qn, preset, en
  Button Reset (.out(Reset_out));
  S_MIPS s_mips_1 (
    .Kbd_Enable(KDB[0]), .Address(Addr), .Kbd_Clear(KDB[1]), .Kbd_Available(KDB[2]), .RAM_In_0(I0),
    .Kbd_ASCII_Data(KDB_DATA), .RAM_In_1(I1), .TTY_Enable(TTY_EN), .RAM_In_2(I2), .RAM_In_3(I3),
    .TTY_ASCII_Data(TTY_DATA), .Reset(RST), .RAM_Out_0(ram_1_data_out_0), .Clock(CLK),
    .RAM_Out_1(ram_1_data_out_1), .Stop(halt), .RAM_Out_2(ram_1_data_out_2), .RAM_Out_3(ram_1_data_out_3),
    .Mask(Mask), .Read_Time(ram_1_read_time), .Write_Time(ram_1_write_time), .nRead_Write(R_W),
    .Chip_Select(CS));
  D_Flip_Flop d_ff_2 (.clk(CLK), .D(d_ff_1_q), .Qn(LCLR), .reset(Reset_out));  // open: Q, preset, en
  or or_1 (RST, LCLR, LoadRAM);
  Clock clock_1 (.out(CLK));
  Multiplexer #(.width(32), .enable("false")) multiplexer_1 (.in0(I0), .in1(LData), .out(RI0), .sel(LoadRAM));
  Multiplexer #(.width(32), .enable("false")) multiplexer_2 (.in0(I1), .in1(LData), .out(RI1), .sel(LoadRAM));
  Multiplexer #(.width(32), .enable("false")) multiplexer_3 (.in0(I2), .in1(LData), .out(RI2), .sel(LoadRAM));
  Multiplexer #(.width(32), .enable("false")) multiplexer_4 (.in0(I3), .in1(LData), .out(RI3), .sel(LoadRAM));
  and and_1 (LoadRAM, ~DESHABILITAR_DISPATCHER, LoadRAMOn);  // AND_Gate
  Multiplexer #(.width(16), .enable("false")) multiplexer_5 (.in0(Addr), .in1(LAddr), .out(RAddr), .sel(LoadRAM));
  Multiplexer #(.width(4), .enable("false")) multiplexer_6 (.in0(Mask), .in1(LMask), .out(RMask), .sel(LoadRAM));
  Multiplexer #(.enable("false")) multiplexer_7 (.in0(CS), .in1(LW), .out(RCS), .sel(LoadRAM));
  Multiplexer #(.enable("false")) multiplexer_8 (.in0(R_W), .in1(LW), .out(R_R_W), .sel(LoadRAM));

  // Notes on the sheet:
  //   NO MODIFICAR
  //   Keyboard
endmodule

module RAM (
  input  [15:0] Address,
  input  [31:0] Data_In_0,
  input  [31:0] Data_In_1,
  input  [31:0] Data_In_2,
  input  [31:0] Data_In_3,
  input  [3:0] Mask,
  input  nRead_Write,
  input  Chip_Select,
  input  Reset,
  output [31:0] Data_Out_0,
  output [31:0] Data_Out_1,
  output [31:0] Data_Out_2,
  output [31:0] Data_Out_3,
  output [3:0] Read_Time,
  output [3:0] Write_Time
);

  wire and_2_out, and_3_out, and_4_out, and_5_out, and_6_out, and_7_out, and_8_out, and_9_out, Changed, CLK,
       comparator_2_eq, comparator_3_eq, comparator_4_eq, comparator_5_eq, comparator_6_eq, Count,
       demultiplexer_3_out0, Idle, Idle_q, Load, Load0, Load1, nand_1_out, or_1_out, or_2_out, or_3_out,
       or_4_out, or_5_out, or_6_out, or_7_out, or_8_out, or_9_out, or_10_out, Proc_q, Update_Mem, Zero_Time;
  wire [3:0] counter_1_q, multiplexer_1_out, subtractor_1_out;
  wire [31:0] register_1_q, register_2_q, register_3_q, register_4_q, register_5_q;

  // Probe on 4'b0011
  // Probe on 4'b0010
  Multiplexer #(.width(4), .enable("false")) multiplexer_1 (
    .in0(4'b0011), .in1(4'b0010), .out(multiplexer_1_out), .sel(nRead_Write));
  or or_1 (or_1_out, Idle, Update_Mem);
  or or_2 (or_2_out, ~Chip_Select, Reset);  // OR_Gate
  Subtractor #(.width(4)) subtractor_1 (.a(multiplexer_1_out), .b(4'b0010), .out(subtractor_1_out));  // open: bin, bout
  Demultiplexer #(.enable("false")) demultiplexer_1 (.out0(Idle), .out1(Load0), .in(Idle_q), .sel(Changed));
  D_Flip_Flop u_Idle (.clk(CLK), .D(or_1_out), .Q(Idle_q), .preset(or_2_out));  // open: Qn, en, reset
  // Probe on counter_1_q
  Counter #(.width(4), .max('hf)) counter_1 (
    .load(Load), .D(subtractor_1_out), .count(Count), .Q(counter_1_q), .clk(CLK), .clr(or_3_out));  // open: carry
  or or_3 (or_3_out, ~Chip_Select, Reset);  // OR_Gate
  Comparator #(.width(4), .mode("unsigned")) comparator_1 (
    .a(4'b0000), .b(counter_1_q), .eq(Zero_Time));  // open: gt, lt
  or or_4 (or_4_out, Count, Load0, Load1);
  Register #(.width(32)) register_1 (.D(Data_In_0), .en(Chip_Select), .Q(register_1_q), .clk(CLK), .clr(or_5_out));
  or or_5 (or_5_out, ~Chip_Select, Reset);  // OR_Gate
  Register #(.width(32)) register_2 (.D(Data_In_1), .en(Chip_Select), .Q(register_2_q), .clk(CLK), .clr(or_6_out));
  or or_6 (or_6_out, ~Chip_Select, Reset);  // OR_Gate
  Register #(.width(32)) register_3 (.D(Data_In_2), .en(Chip_Select), .Q(register_3_q), .clk(CLK), .clr(or_7_out));
  or or_7 (or_7_out, ~Chip_Select, Reset);  // OR_Gate
  Register #(.width(32)) register_4 (.D(Data_In_3), .en(Chip_Select), .Q(register_4_q), .clk(CLK), .clr(or_8_out));
  or or_8 (or_8_out, ~Chip_Select, Reset);  // OR_Gate
  Register #(.width(32)) register_5 (
    .D({{11{1'b1}}, nRead_Write, Mask, Address}), .en(Chip_Select), .Q(register_5_q), .clk(CLK),
    .clr(or_9_out));
  or or_9 (or_9_out, ~Chip_Select, Reset);  // OR_Gate
  D_Flip_Flop Proc (.clk(CLK), .D(or_4_out), .Q(Proc_q), .reset(or_10_out));  // open: Qn, preset, en
  or or_10 (or_10_out, ~Chip_Select, Reset);  // OR_Gate
  Demultiplexer #(.enable("false")) demultiplexer_2 (
    .out0(Count), .out1(Update_Mem), .in(demultiplexer_3_out0), .sel(Zero_Time));
  Demultiplexer #(.enable("false")) demultiplexer_3 (
    .out0(demultiplexer_3_out0), .out1(Load1), .in(Proc_q), .sel(Changed));
  Clock clock_1 (.out(CLK));
  Comparator #(.width(32)) comparator_2 (.a(register_1_q), .b(Data_In_0), .eq(comparator_2_eq));  // open: gt, lt
  Comparator #(.width(32)) comparator_3 (.a(register_2_q), .b(Data_In_1), .eq(comparator_3_eq));  // open: gt, lt
  Comparator #(.width(32)) comparator_4 (.a(register_3_q), .b(Data_In_2), .eq(comparator_4_eq));  // open: gt, lt
  Comparator #(.width(32)) comparator_5 (.a(register_4_q), .b(Data_In_3), .eq(comparator_5_eq));  // open: gt, lt
  Comparator #(.width(32)) comparator_6 (
    .a(register_5_q), .b({{11{1'b1}}, nRead_Write, Mask, Address}), .eq(comparator_6_eq));  // open: gt, lt
  nand nand_1 (nand_1_out, comparator_6_eq, comparator_2_eq, comparator_3_eq, comparator_4_eq, comparator_5_eq);
  and and_1 (Changed, nand_1_out, Chip_Select);
  or or_11 (Load, Count, Load1, Load0);
  and and_2 (and_2_out, Mask[0], Update_Mem, nRead_Write);
  and and_3 (and_3_out, Mask[1], Update_Mem, nRead_Write);
  and and_4 (and_4_out, Mask[2], Update_Mem, nRead_Write);
  and and_5 (and_5_out, Mask[3], Update_Mem, nRead_Write);
  RAM_part #(.addrWidth(16), .dataWidth(32), .bus("separate")) ram_1 (
    .addr(Address), .din(Data_In_0), .data(Data_Out_0), .str(and_2_out), .sel(Chip_Select), .clk(CLK),
    .ld(and_6_out), .clr(Reset));
  and and_6 (and_6_out, ~nRead_Write, Idle);  // AND_Gate
  RAM_part #(.addrWidth(16), .dataWidth(32), .bus("separate")) ram_2 (
    .addr(Address), .din(Data_In_1), .data(Data_Out_1), .str(and_3_out), .sel(Chip_Select), .clk(CLK),
    .ld(and_7_out), .clr(Reset));
  and and_7 (and_7_out, ~nRead_Write, Idle);  // AND_Gate
  RAM_part #(.addrWidth(16), .dataWidth(32), .bus("separate")) ram_3 (
    .addr(Address), .din(Data_In_2), .data(Data_Out_2), .str(and_4_out), .sel(Chip_Select), .clk(CLK),
    .ld(and_8_out), .clr(Reset));
  and and_8 (and_8_out, ~nRead_Write, Idle);  // AND_Gate
  RAM_part #(.addrWidth(16), .dataWidth(32), .bus("separate")) ram_4 (
    .addr(Address), .din(Data_In_3), .data(Data_Out_3), .str(and_5_out), .sel(Chip_Select), .clk(CLK),
    .ld(and_9_out), .clr(Reset));
  and and_9 (and_9_out, ~nRead_Write, Idle);  // AND_Gate

  assign Read_Time = 4'b0011;
  assign Write_Time = 4'b0010;

  // Other names for the same wires on the sheet: M0 = Mask[0]; M1 = Mask[1]; M2 = Mask[2]; M3 = Mask[3];
  //   RW = nRead_Write; CLR = Reset; CS = Chip_Select; Load2 = Count

  // Notes on the sheet:
  //   NO MODIFICAR
  //   excepto quizás los valores RT y WT
  //   BANK0
  //   BANK1
  //   BANK2
  //   BANK3
endmodule

module S_MIPS (
  input  Kbd_Available,
  input  [6:0] Kbd_ASCII_Data,
  input  [31:0] RAM_Out_0,
  input  [31:0] RAM_Out_1,
  input  Reset,
  input  [31:0] RAM_Out_2,
  input  Clock,
  input  [31:0] RAM_Out_3,
  input  [3:0] Read_Time,
  input  [3:0] Write_Time,
  output Kbd_Enable,
  output [15:0] Address,
  output Kbd_Clear,
  output TTY_Enable,
  output [6:0] TTY_ASCII_Data,
  output Stop,
  output [31:0] RAM_In_0,
  output [31:0] RAM_In_1,
  output [31:0] RAM_In_2,
  output [31:0] RAM_In_3,
  output [3:0] Mask,
  output nRead_Write,
  output Chip_Select
);

  wire ALUI, d_ff_2_q, EnablerGI, EnablerPC, EnablerRF, GetData, Getl, Halt, Jumpl, Memoryl, Memoryl_star,
       or_1_out, ReadyData, Readyl, ReadyW, RI, Stackl, Start, Tty, Write, Writel;
  wire [31:0] Address_t, Bank0, Bank1, Bank2, Bank3, BankOut0, BankOut1, BankOut2, BankOut3,
       data_path_1_rout, DataIn;

  D_Flip_Flop #(.trigger("falling")) d_ff_1 (.clk(Clock), .D(Reset), .Q(Start));  // open: Qn, preset, en, reset
  Multiplexer #(.width(32), .enable("false")) multiplexer_1 (.in0(RAM_Out_0), .in1(RAM_In_0), .out(Bank0), .sel(Write));
  Multiplexer #(.width(32), .enable("false")) multiplexer_2 (.in0(RAM_Out_1), .in1(RAM_In_0), .out(Bank1), .sel(Write));
  Multiplexer #(.width(32), .enable("false")) multiplexer_3 (.in0(RAM_Out_2), .in1(RAM_In_0), .out(Bank2), .sel(Write));
  Multiplexer #(.width(32), .enable("false")) multiplexer_4 (.in0(RAM_Out_3), .in1(RAM_In_0), .out(Bank3), .sel(Write));
  D_Flip_Flop #(.trigger("falling")) d_ff_2 (
    .clk(Clock), .D(Getl), .Q(d_ff_2_q), .en(or_1_out));  // open: Qn, preset, reset
  or or_1 (or_1_out, Getl, Readyl);
  Control_Unit control_unit_1 (
    .Clk(Clock), .ReadyData(ReadyData), .Reset(Reset), .ReadyI(Readyl), .Start(Start), .ReadyW(ReadyW),
    .MemoryI(Memoryl_star), .RI(RI), .Altul(ALUI), .JumpI(Jumpl), .GetI(Getl), .WriteI(Writel), .Ttyl(Tty),
    .Write(Write), .GetData(GetData), .End(Stop), .UseRF(EnablerRF), .UseGI(EnablerGI), .TtyEn(TTY_Enable),
    .KeyboardEn(Kbd_Enable), .UsePC(EnablerPC));
  I_O i_o_1 (.in_1(data_path_1_rout), .Output(RAM_In_0));
  Data_Path data_path_1 (
    .in_1(DataIn), .in_2(Clock), .in_3(Kbd_Available), .in_4(d_ff_2_q), .in_5(Reset), .in_6(EnablerPC),
    .in_7(EnablerRF), .in_8(EnablerGI), .in_9(Kbd_ASCII_Data), .Write(Writel), .ALUI(ALUI), .Stack(Stackl),
    .Memory(Memoryl), .Tty(Tty), .Jump(Jumpl), .RI(RI), .Halt(Halt), .Address(Address_t),
    .TtyData(TTY_ASCII_Data), .ROut(data_path_1_rout));
  RamI rami_1 (
    .Bank_0(Bank0), .Bank_1(Bank1), .Bank_2(Bank2), .Bank_3(Bank3), .DPAddress(Address_t), .Mask(Mask),
    .in_6(Read_Time), .in_7(Clock), .in_8(Reset), .in_9(Getl), .in_10(Write), .in_11(GetData),
    .in_12(EnablerGI), .WriteTime(Write_Time), .ADDR(Address), .BankOut_0(BankOut0), .BankOut_1(BankOut1),
    .BankOut_2(BankOut2), .BankOut_3(BankOut3), .Ready(Readyl), .CS(Chip_Select), .RW(nRead_Write),
    .ReadyData(ReadyData), .ReadyWrite(ReadyW));
  // Probe on BankOut3
  or or_2 (Memoryl_star, Memoryl, Stackl);
  // Probe on DataIn
  Multiplexer #(.select(2), .width(32), .enable("false")) multiplexer_5 (
    .in0(BankOut0), .in1(BankOut1), .in2(BankOut2), .in3(BankOut3), .out(DataIn), .sel(Address_t[3:2]));

  assign Kbd_Clear = Reset;
  assign RAM_In_1 = RAM_In_0;
  assign RAM_In_2 = RAM_In_0;
  assign RAM_In_3 = RAM_In_0;

  // Other names for the same wires on the sheet: CLK = Clock; CS = Chip_Select; KBD_AVAIL = Kbd_Available;
  //   CLR = Reset; KBD_CLR = Reset; KBD_DATA[6:0] = Kbd_ASCII_Data; RAM_A[15:0] = Address; RAM_MASK[3:0] = Mask;
  //   RAM_OUTPUT_0[31:0] = RAM_Out_0; RAM_OUTPUT_1[31:0] = RAM_Out_1; RAM_OUTPUT_2[31:0] = RAM_Out_2;
  //   RAM_OUTPUT_3[31:0] = RAM_Out_3; RAM_INPUT_0[31:0] = RAM_In_0; RAM_INPUT_1[31:0] = RAM_In_0;
  //   RAM_INPUT_2[31:0] = RAM_In_0; RAM_INPUT_3[31:0] = RAM_In_0; ROut[31:0] = RAM_In_0; RW = nRead_Write;
  //   TTY_DATA[6:0] = TTY_ASCII_Data

  // Notes on the sheet:
  //   RAM ADDRESS
  //   DATA FROM RAM
  //   DATA TO RAM
  //   DATA WRITE MASK
  //   RAM TIMING
  //   RAM CONTROL
  //   KEYBOARD
  //   TTY
  //   SEQUENCING
endmodule

module RAM_Dispatcher (
  input  [3:0] WriteTime,
  input  Clock,
  input  CLR,
  output [31:0] Data,
  output [15:0] Address,
  output [3:0] Mask,
  output Finished,
  output Write
);

  wire demultiplexer_2_out1, demultiplexer_3_out1, End, IDLE_q, IncAddr, Load, or_1_out, or_2_out, While_q,
       WriteEnd;
  wire [3:0] counter_1_q;
  wire [31:0] CurrentAddress_q;

  Counter #(.width(32), .max('hffffffff)) CurrentAddress (
    .count(IncAddr), .Q({CurrentAddress_q[31:18], Address, CurrentAddress_q[1:0]}), .clk(Clock), .clr(CLR));  // open: load, D, carry
  or or_1 (or_1_out, IncAddr, demultiplexer_3_out1, Finished);
  D_Flip_Flop IDLE (.clk(Clock), .D(or_1_out), .Q(IDLE_q), .preset(CLR));  // open: Qn, en, reset
  Demultiplexer #(.enable("false")) demultiplexer_1 (.out0(Load), .out1(Finished), .in(IDLE_q), .sel(End));
  D_Flip_Flop While (.clk(Clock), .D(or_2_out), .Q(While_q), .reset(CLR));  // open: Qn, preset, en
  or or_2 (or_2_out, Write, Load);
  RAM_part #(.addrWidth(18), .dataWidth(32)) ram_1 (
    .addr({Address, CurrentAddress_q[1:0]}), .data(Data), .clk(Clock));  // open: sel, ld, clr
  Demultiplexer #(.enable("false")) demultiplexer_2 (
    .out0(Write), .out1(demultiplexer_2_out1), .in(While_q), .sel(WriteEnd));
  Decoder #(.select(2)) decoder_1 (
    .out0(Mask[0]), .out1(Mask[1]), .out2(Mask[2]), .out3(Mask[3]), .sel(CurrentAddress_q[1:0]));  // open: en
  Demultiplexer #(.enable("false")) demultiplexer_3 (
    .out0(IncAddr), .out1(demultiplexer_3_out1), .in(demultiplexer_2_out1), .sel(End));
  Counter #(.width(4), .max('hf)) counter_1 (
    .load(Load), .D(WriteTime), .count(Write), .Q(counter_1_q), .clk(Clock));  // open: carry, clr
  Comparator #(.width(32)) comparator_1 (.a(Data), .b({32{1'b1}}), .eq(End));  // open: gt, lt
  Comparator #(.width(4)) comparator_2 (.a(4'b0000), .b(counter_1_q), .eq(WriteEnd));  // open: gt, lt

  // Other names for the same wires on the sheet: CLK = Clock; Count = Write; WT[3:0] = WriteTime
endmodule

// RF
module Register_File (
  input  in_1,
  input  in_2,
  input  [31:0] in_3,
  input  in_4,
  input  in_5,
  input  in_6,
  input  in_7,
  input  [4:0] Destination,
  input  [4:0] in_9,
  input  [4:0] in_10,
  output [31:0] Stack_Pointer,
  output [31:0] Output_A,
  output [31:0] Output_B
);

  wire and_1_out, EN_32, or_1_out, R1, R2, R3, R4, R5, R6, R7, R8, R9, R10, R11, R12, R13, R14, R15, R16,
       R17, R18, R19, R20, R21, R22, R23, R24, R25, R26, R27, R28, R29, R30, R31, R32;
  wire [31:0] adder_1_out, multiplexer_2_out, multiplexer_3_out, multiplexer_4_out, O1, O2, O3, O4, O5, O6,
       O7, O8, O9, O10, O11, O12, O13, O14, O15, O16, O17, O18, O19, O20, O21, O22, O23, O24, O25, O26, O27,
       O28, O29, O30, O31, subtractor_1_out;

  Demultiplexer #(.select(5), .enable("false")) demultiplexer_1 (
    .out0(R1), .out1(R2), .out2(R3), .out3(R4), .out4(R5), .out5(R6), .out6(R7), .out7(R8), .out8(R9),
    .out9(R10), .out10(R11), .out11(R12), .out12(R13), .out13(R14), .out14(R15), .out15(R16), .out16(R17),
    .out17(R18), .out18(R19), .out19(R20), .out20(R21), .out21(R22), .out22(R23), .out23(R24), .out24(R25),
    .out25(R26), .out26(R27), .out27(R28), .out28(R29), .out29(R30), .out30(R31), .out31(R32), .in(in_6),
    .sel(Destination));
  Multiplexer #(.select(5), .width(32), .enable("false")) multiplexer_1 (
    .in0(O1), .in1(O2), .in2(O3), .in3(O4), .in4(O5), .in5(O6), .in6(O7), .in7(O8), .in8(O9), .in9(O10),
    .in10(O11), .in11(O12), .in12(O13), .in13(O14), .in14(O15), .in15(O16), .in16(O17), .in17(O18),
    .in18(O19), .in19(O20), .in20(O21), .in21(O22), .in22(O23), .in23(O24), .in24(O25), .in25(O26),
    .in26(O27), .in27(O28), .in28(O29), .in29(O30), .in30(O31), .in31(Stack_Pointer), .out(Output_A),
    .sel(in_9));
  Adder #(.width(32)) adder_1 (.a(Stack_Pointer), .b(32'h4), .out(adder_1_out));  // open: cin, cout
  Subtractor #(.width(32)) subtractor_1 (.a(Stack_Pointer), .b(32'h4), .out(subtractor_1_out));  // open: bin, bout
  Register #(.width(32)) register_1 (.D(in_3), .en(R1), .Q(O1), .clk(in_1), .clr(in_4));
  Register #(.width(32)) register_2 (.D(in_3), .en(R9), .Q(O9), .clk(in_1), .clr(in_4));
  Register #(.width(32)) register_3 (.D(in_3), .en(R17), .Q(O17), .clk(in_1), .clr(in_4));
  Register #(.width(32)) register_4 (.D(in_3), .en(R25), .Q(O25), .clk(in_1), .clr(in_4));
  Multiplexer #(.width(32), .enable("false")) multiplexer_2 (
    .in0(adder_1_out), .in1(subtractor_1_out), .out(multiplexer_2_out), .sel(in_7));
  Multiplexer #(.width(32), .enable("false")) multiplexer_3 (
    .in0(multiplexer_2_out), .in1({32{1'b1}}), .out(multiplexer_3_out), .sel(in_4));
  Register #(.width(32)) register_5 (.D(in_3), .en(R2), .Q(O2), .clk(in_1), .clr(in_4));
  Register #(.width(32)) register_6 (.D(in_3), .en(R10), .Q(O10), .clk(in_1), .clr(in_4));
  Register #(.width(32)) register_7 (.D(in_3), .en(R18), .Q(O18), .clk(in_1), .clr(in_4));
  Register #(.width(32)) register_8 (.D(in_3), .en(R26), .Q(O26), .clk(in_1), .clr(in_4));
  Multiplexer #(.width(32), .enable("false")) multiplexer_4 (
    .in0(multiplexer_3_out), .in1(in_3), .out(multiplexer_4_out), .sel(R32));
  Register #(.width(32)) register_9 (.D(in_3), .en(R3), .Q(O3), .clk(in_1), .clr(in_4));
  Register #(.width(32)) register_10 (.D(in_3), .en(R11), .Q(O11), .clk(in_1), .clr(in_4));
  Register #(.width(32)) register_11 (.D(in_3), .en(R19), .Q(O19), .clk(in_1), .clr(in_4));
  Register #(.width(32)) register_12 (.D(in_3), .en(R27), .Q(O27), .clk(in_1), .clr(in_4));
  Multiplexer #(.select(5), .width(32), .enable("false")) multiplexer_5 (
    .in0(O1), .in1(O2), .in2(O3), .in3(O4), .in4(O5), .in5(O6), .in6(O7), .in7(O8), .in8(O9), .in9(O10),
    .in10(O11), .in11(O12), .in12(O13), .in13(O14), .in14(O15), .in15(O16), .in16(O17), .in17(O18),
    .in18(O19), .in19(O20), .in20(O21), .in21(O22), .in22(O23), .in23(O24), .in24(O25), .in25(O26),
    .in26(O27), .in27(O28), .in28(O29), .in29(O30), .in30(O31), .in31(Stack_Pointer), .out(Output_B),
    .sel(in_10));
  Register #(.width(32)) register_13 (.D(multiplexer_4_out), .en(EN_32), .Q(Stack_Pointer), .clk(in_1));  // open: clr
  or or_1 (or_1_out, in_7, in_2);
  Register #(.width(32)) register_14 (.D(in_3), .en(R4), .Q(O4), .clk(in_1), .clr(in_4));
  Register #(.width(32)) register_15 (.D(in_3), .en(R12), .Q(O12), .clk(in_1), .clr(in_4));
  Register #(.width(32)) register_16 (.D(in_3), .en(R20), .Q(O20), .clk(in_1), .clr(in_4));
  Register #(.width(32)) register_17 (.D(in_3), .en(R28), .Q(O28), .clk(in_1), .clr(in_4));
  and and_1 (and_1_out, or_1_out, in_5);
  Register #(.width(32)) register_18 (.D(in_3), .en(R5), .Q(O5), .clk(in_1), .clr(in_4));
  Register #(.width(32)) register_19 (.D(in_3), .en(R13), .Q(O13), .clk(in_1), .clr(in_4));
  Register #(.width(32)) register_20 (.D(in_3), .en(R21), .Q(O21), .clk(in_1), .clr(in_4));
  Register #(.width(32)) register_21 (.D(in_3), .en(R29), .Q(O29), .clk(in_1), .clr(in_4));
  or or_2 (EN_32, R32, and_1_out, in_4);
  Register #(.width(32)) register_22 (.D(in_3), .en(R6), .Q(O6), .clk(in_1), .clr(in_4));
  Register #(.width(32)) register_23 (.D(in_3), .en(R14), .Q(O14), .clk(in_1), .clr(in_4));
  Register #(.width(32)) register_24 (.D(in_3), .en(R22), .Q(O22), .clk(in_1), .clr(in_4));
  Register #(.width(32)) register_25 (.D(in_3), .en(R30), .Q(O30), .clk(in_1), .clr(in_4));
  Register #(.width(32)) register_26 (.D(in_3), .en(R7), .Q(O7), .clk(in_1), .clr(in_4));
  Register #(.width(32)) register_27 (.D(in_3), .en(R15), .Q(O15), .clk(in_1), .clr(in_4));
  Register #(.width(32)) register_28 (.D(in_3), .en(R23), .Q(O23), .clk(in_1), .clr(in_4));
  Register #(.width(32)) register_29 (.D(in_3), .en(R31), .Q(O31), .clk(in_1), .clr(in_4));
  Register #(.width(32)) register_30 (.D(in_3), .en(R8), .Q(O8), .clk(in_1), .clr(in_4));
  Register #(.width(32)) register_31 (.D(in_3), .en(R16), .Q(O16), .clk(in_1), .clr(in_4));
  Register #(.width(32)) register_32 (.D(in_3), .en(R24), .Q(O24), .clk(in_1), .clr(in_4));

  // Other names for the same wires on the sheet: clk = in_1; dest[4:0] = Destination; Input[31:0] = in_3;
  //   O32[31:0] = Stack_Pointer; PCenable = in_5; pop = in_7; push = in_2; reset = in_4; Select_A[4:0] = in_9;
  //   Select_B[4:0] = in_10; write = in_6
endmodule

module SLT (
  input  [31:0] A,
  input  [31:0] B,
  input  in_3,
  output [31:0] Output
);

  wire and_1_out, and_2_out, comparator_1_lt, comparator_2_lt;

  Comparator #(.width(32)) comparator_1 (.a(A), .b(B), .lt(comparator_1_lt));  // open: gt, eq
  Comparator #(.width(32)) comparator_2 (.a(A), .b(B), .lt(comparator_2_lt));  // open: gt, eq
  and and_1 (and_1_out, comparator_1_lt, in_3);
  and and_2 (and_2_out, in_3, comparator_2_lt);
  or or_1 (Output[0], and_1_out, and_2_out);

  assign Output[31:1] = {31{1'b0}};

  // Other names for the same wires on the sheet: NoSign = in_3; IsLess = Output[0]
endmodule

module Mult (
  input  [31:0] A,
  input  [31:0] B,
  input  in_3,
  output [31:0] Output,
  output [31:0] Output_2
);

  wire adder_1_cout, Sel, SignA, SignB, xor_1_out;
  wire [31:0] AbsA, AbsB, bit_extender_1_out, HI, HIC2, LO, LOC2, not_1_out, not_2_out;

  Absolute absolute_1 (.in_1(A), .in_2(in_3), .Output_2(SignA), .Output(AbsA));
  Absolute absolute_2 (.in_1(B), .in_2(in_3), .Output_2(SignB), .Output(AbsB));
  xor xor_1 (xor_1_out, SignA, SignB);
  Multiplier #(.width(32)) multiplier_1 (.a(AbsA), .b(AbsB), .out(LO), .cout(HI));  // open: cin
  Multiplexer #(.width(32), .enable("false")) multiplexer_1 (.in0(LO), .in1(LOC2), .out(Output), .sel(Sel));
  Multiplexer #(.width(32), .enable("false")) multiplexer_2 (.in0(HI), .in1(HIC2), .out(Output_2), .sel(Sel));
  and and_1 (Sel, ~in_3, xor_1_out);  // AND_Gate
  assign not_1_out = ~LO;  // NOT_Gate not_1, 32 bits wide
  Adder #(.width(32)) adder_1 (.a(not_1_out), .b(32'h1), .out(LOC2), .cout(adder_1_cout));  // open: cin
  assign bit_extender_1_out = {{31{1'b0}}, adder_1_cout};  // Bit_Extender bit_extender_1
  assign not_2_out = ~HI;  // NOT_Gate not_2, 32 bits wide
  Adder #(.width(32)) adder_2 (.a(not_2_out), .b(bit_extender_1_out), .out(HIC2));  // open: cin, cout

  // Other names for the same wires on the sheet: NoSign = in_3; OutHI[31:0] = Output_2; OutLO[31:0] = Output
endmodule

module Absolute (
  input  [31:0] in_1,
  input  in_2,
  output [31:0] Output,
  output Output_2
);

  wire and_1_out;
  wire [31:0] negator_1_out;

  Negator #(.width(32)) negator_1 (.in(in_1), .out(negator_1_out));
  Multiplexer #(.width(32), .enable("false")) multiplexer_1 (
    .in0(in_1), .in1(negator_1_out), .out(Output), .sel(and_1_out));
  buf and_1 (and_1_out, in_1[31]);  // AND_Gate AND_Gate

  assign Output_2 = in_1[31];

  // Other names for the same wires on the sheet: Bit31 = in_1[31]; NoSign = in_2
endmodule

// DIV
module Div (
  input  [31:0] A,
  input  [31:0] B,
  input  in_3,
  output [31:0] Output_LO,
  output [31:0] Output_HI
);

  wire [31:0] HIS, HIU, LOS, LOU, multiplexer_1_out, multiplexer_2_out, negator_1_out, negator_2_out;

  Negator #(.width(32)) negator_1 (.in(A), .out(negator_1_out));
  Negator #(.width(32)) negator_2 (.in(B), .out(negator_2_out));
  Divider #(.width(32)) divider_1 (.a(A), .b(B), .out(LOU), .rem(HIU));  // open: upper
  Multiplexer #(.width(32), .enable("false")) multiplexer_1 (
    .in0(A), .in1(negator_1_out), .out(multiplexer_1_out), .sel(A[31]));
  Multiplexer #(.width(32), .enable("false")) multiplexer_2 (
    .in0(B), .in1(negator_2_out), .out(multiplexer_2_out), .sel(B[31]));
  Divider #(.width(32)) divider_2 (.a(multiplexer_1_out), .b(multiplexer_2_out), .out(LOS), .rem(HIS));  // open: upper
  Multiplexer #(.width(32), .enable("false")) multiplexer_3 (.in0(LOS), .in1(LOU), .out(Output_LO), .sel(in_3));
  Multiplexer #(.width(32), .enable("false")) multiplexer_4 (.in0(HIS), .in1(HIU), .out(Output_HI), .sel(in_3));
  Divider #(.width(32)) divider_3 ();  // open: a, b, out, upper, rem

  // Other names for the same wires on the sheet: SignA = A[31]; SignB = B[31]; NoSign = in_3
endmodule

module ALU (
  input  in_1,
  input  [31:0] A,
  input  in_3,
  input  [31:0] B,
  input  in_5,
  input  [3:0] in_6,
  output [31:0] Output,
  output [31:0] Output_2,
  output [31:0] Output_3
);

  wire Div, Enable, Mult, or_2_out;
  wire [31:0] Add, And, DivHI, DivLO, MultHI, multiplexer_2_out, multiplexer_3_out, MultLO, Nor, Or, Slt,
       Subs, Xor;

  Adder #(.width(32)) adder_1 (.a(A), .b(B), .out(Add));  // open: cin, cout
  Subtractor #(.width(32)) subtractor_1 (.a(A), .b(B), .out(Subs));  // open: bin, bout
  assign And = A & B;  // AND_Gate and_1, 32 bits wide
  assign Or = A | B;  // OR_Gate or_1, 32 bits wide
  assign Nor = ~(A | B);  // NOR_Gate nor_1, 32 bits wide
  assign Xor = A ^ B;  // XOR_Gate xor_1, 32 bits wide
  SLT slt_1 (.A(A), .B(B), .in_3(in_5), .Output(Slt));
  Mult mult_1 (.A(A), .B(B), .in_3(in_5), .Output(MultLO), .Output_2(MultHI));
  Div div_1 (.A(A), .B(B), .in_3(in_5), .Output_LO(DivLO), .Output_HI(DivHI));
  Multiplexer #(.select(4), .width(32), .enable("false")) multiplexer_1 (
    .in0(Add), .in1(Subs), .in2(And), .in3(Or), .in4(Nor), .in5(Xor), .in6(Slt), .out(Output_2), .sel(in_6));  // open: in7, in8, in9, in10, in11, in12, in13, in14, in15
  Comparator #(.width(4)) comparator_1 (.a(in_6), .b(4'b0000), .eq(Mult));  // open: gt, lt
  Comparator #(.width(4)) comparator_2 (.a(in_6), .b(4'b1111), .eq(Div));  // open: gt, lt
  Multiplexer #(.width(32), .enable("false")) multiplexer_2 (
    .in0(MultLO), .in1(DivLO), .out(multiplexer_2_out), .sel(Div));
  Multiplexer #(.width(32), .enable("false")) multiplexer_3 (
    .in0(MultHI), .in1(DivHI), .out(multiplexer_3_out), .sel(Div));
  or or_2 (or_2_out, Mult, Div);
  Register #(.width(32)) register_1 (.D(multiplexer_2_out), .en(Enable), .Q(Output), .clk(in_1));  // open: clr
  Register #(.width(32)) register_2 (.D(multiplexer_3_out), .en(Enable), .Q(Output_3), .clk(in_1));  // open: clr
  and and_2 (Enable, or_2_out, in_3);

  // Other names for the same wires on the sheet: clk = in_1; HI[31:0] = Output_3; LO[31:0] = Output; NoSign = in_5;
  //   On = in_3; OPSelect[3:0] = in_6
endmodule

// PC
module Program_Counter (
  input  [31:0] in_1,
  input  in_2,
  input  in_3,
  input  in_4,
  output [31:0] Output
);

  Register #(.width(32)) register_1 (.D(in_1), .en(in_4), .Q(Output), .clk(in_2), .clr(in_3));
endmodule

module Instruction_Decoder (
  input  [31:0] in_1,
  output out_2,
  output out_3,
  output out_4,
  output out_5,
  output out_6,
  output out_7,
  output out_8,
  output out_9,
  output out_10,
  output out_11,
  output [25:0] DestJump,
  output out_13,
  output out_14,
  output out_15,
  output out_16,
  output out_17,
  output out_18,
  output out_19,
  output out_20,
  output out_21,
  output out_22,
  output [15:0] Const,
  output out_24,
  output out_25,
  output out_26,
  output out_27,
  output [4:0] Rs,
  output out_29,
  output out_30,
  output out_31,
  output out_32,
  output [4:0] Rt,
  output out_34,
  output out_35,
  output out_36,
  output out_37,
  output [4:0] Rd,
  output out_39,
  output out_40,
  output out_41,
  output out_42
);

  wire comparator_2_eq, comparator_3_eq, comparator_4_eq, comparator_5_eq, comparator_6_eq, comparator_7_eq,
       comparator_8_eq, comparator_11_eq, comparator_12_eq, comparator_13_eq, comparator_14_eq,
       comparator_15_eq, comparator_16_eq, comparator_17_eq, comparator_18_eq, comparator_19_eq,
       comparator_20_eq, comparator_21_eq, comparator_22_eq, comparator_23_eq, comparator_24_eq,
       comparator_25_eq, OP0, OP3F, OP38;

  Comparator #(.width(6)) comparator_1 (.a(in_1[31:26]), .b({6{1'b0}}), .eq(OP0));  // open: gt, lt
  Comparator #(.width(6)) comparator_2 (.a(in_1[5:0]), .b({6{1'b0}}), .eq(comparator_2_eq));  // open: gt, lt
  Comparator #(.width(6)) comparator_3 (.a(in_1[5:0]), .b(6'b100000), .eq(comparator_3_eq));  // open: gt, lt
  Comparator #(.width(6)) comparator_4 (.a(in_1[5:0]), .b(6'b100010), .eq(comparator_4_eq));  // open: gt, lt
  Comparator #(.width(6)) comparator_5 (.a(in_1[5:0]), .b(6'b011000), .eq(comparator_5_eq));  // open: gt, lt
  Comparator #(.width(6)) comparator_6 (.a(in_1[5:0]), .b(6'b011010), .eq(comparator_6_eq));  // open: gt, lt
  Comparator #(.width(6)) comparator_7 (.a(in_1[5:0]), .b(6'b011001), .eq(comparator_7_eq));  // open: gt, lt
  Comparator #(.width(6)) comparator_8 (.a(in_1[5:0]), .b(6'b011011), .eq(comparator_8_eq));  // open: gt, lt
  and and_1 (out_2, OP0, comparator_2_eq);
  and and_2 (out_7, OP0, comparator_3_eq);
  and and_3 (out_13, OP0, comparator_4_eq);
  and and_4 (out_18, OP0, comparator_5_eq);
  and and_5 (out_24, OP0, comparator_6_eq);
  and and_6 (out_29, OP0, comparator_7_eq);
  and and_7 (out_34, OP0, comparator_8_eq);
  Comparator #(.width(6)) comparator_9 (.a(in_1[31:26]), .b({6{1'b1}}), .eq(OP3F));  // open: gt, lt
  Comparator #(.width(6)) comparator_10 (.a(in_1[31:26]), .b(6'b111000), .eq(OP38));  // open: gt, lt
  and and_8 (out_39, OP0, comparator_11_eq);
  Comparator #(.width(6)) comparator_11 (.a(in_1[5:0]), .b(6'b101010), .eq(comparator_11_eq));  // open: gt, lt
  and and_9 (out_3, OP0, comparator_12_eq);
  Comparator #(.width(6)) comparator_12 (.a(in_1[5:0]), .b(6'b101011), .eq(comparator_12_eq));  // open: gt, lt
  and and_10 (out_8, OP0, comparator_13_eq);
  Comparator #(.width(6)) comparator_13 (.a(in_1[5:0]), .b(6'b100100), .eq(comparator_13_eq));  // open: gt, lt
  and and_11 (out_14, OP0, comparator_14_eq);
  Comparator #(.width(6)) comparator_14 (.a(in_1[5:0]), .b(6'b100101), .eq(comparator_14_eq));  // open: gt, lt
  and and_12 (out_19, OP0, comparator_15_eq);
  Comparator #(.width(6)) comparator_15 (.a(in_1[5:0]), .b(6'b100111), .eq(comparator_15_eq));  // open: gt, lt
  and and_13 (out_25, OP0, comparator_16_eq);
  Comparator #(.width(6)) comparator_16 (.a(in_1[5:0]), .b(6'b101000), .eq(comparator_16_eq));  // open: gt, lt
  and and_14 (out_30, OP38, comparator_17_eq);
  Comparator #(.width(6)) comparator_17 (.a(in_1[5:0]), .b({6{1'b0}}), .eq(comparator_17_eq));  // open: gt, lt
  and and_15 (out_35, OP38, comparator_18_eq);
  Comparator #(.width(6)) comparator_18 (.a(in_1[5:0]), .b(6'b000001), .eq(comparator_18_eq));  // open: gt, lt
  and and_16 (out_40, OP0, comparator_19_eq);
  Comparator #(.width(6)) comparator_19 (.a(in_1[5:0]), .b(6'b001000), .eq(comparator_19_eq));  // open: gt, lt
  and and_17 (out_4, OP0, comparator_20_eq);
  Comparator #(.width(6)) comparator_20 (.a(in_1[5:0]), .b(6'b010000), .eq(comparator_20_eq));  // open: gt, lt
  and and_18 (out_9, OP0, comparator_21_eq);
  Comparator #(.width(6)) comparator_21 (.a(in_1[5:0]), .b(6'b010010), .eq(comparator_21_eq));  // open: gt, lt
  and and_19 (out_15, OP3F, comparator_22_eq);
  Comparator #(.width(6)) comparator_22 (.a(in_1[5:0]), .b({6{1'b1}}), .eq(comparator_22_eq));  // open: gt, lt
  and and_20 (out_20, OP3F, comparator_23_eq);
  Comparator #(.width(6)) comparator_23 (.a(in_1[5:0]), .b(6'b000001), .eq(comparator_23_eq));  // open: gt, lt
  and and_21 (out_26, OP3F, comparator_24_eq);
  Comparator #(.width(6)) comparator_24 (.a(in_1[5:0]), .b(6'b000010), .eq(comparator_24_eq));  // open: gt, lt
  and and_22 (out_31, OP3F, comparator_25_eq);
  Comparator #(.width(6)) comparator_25 (.a(in_1[5:0]), .b(6'b000100), .eq(comparator_25_eq));  // open: gt, lt
  Comparator #(.width(6)) comparator_26 (.a(in_1[31:26]), .b(6'b001000), .eq(out_36));  // open: gt, lt
  Comparator #(.width(6)) comparator_27 (.a(in_1[31:26]), .b(6'b001010), .eq(out_41));  // open: gt, lt
  Comparator #(.width(6)) comparator_28 (.a(in_1[31:26]), .b(6'b001011), .eq(out_5));  // open: gt, lt
  Comparator #(.width(6)) comparator_29 (.a(in_1[31:26]), .b(6'b001100), .eq(out_10));  // open: gt, lt
  Comparator #(.width(6)) comparator_30 (.a(in_1[31:26]), .b(6'b001101), .eq(out_16));  // open: gt, lt
  Comparator #(.width(6)) comparator_31 (.a(in_1[31:26]), .b(6'b001110), .eq(out_21));  // open: gt, lt
  Comparator #(.width(6)) comparator_32 (.a(in_1[31:26]), .b(6'b100011), .eq(out_27));  // open: gt, lt
  Comparator #(.width(6)) comparator_33 (.a(in_1[31:26]), .b(6'b101011), .eq(out_32));  // open: gt, lt
  Comparator #(.width(6)) comparator_34 (.a(in_1[31:26]), .b(6'b000100), .eq(out_37));  // open: gt, lt
  Comparator #(.width(6)) comparator_35 (.a(in_1[31:26]), .b(6'b000101), .eq(out_42));  // open: gt, lt
  Comparator #(.width(6)) comparator_36 (.a(in_1[31:26]), .b(6'b000110), .eq(out_6));  // open: gt, lt
  Comparator #(.width(6)) comparator_37 (.a(in_1[31:26]), .b(6'b000111), .eq(out_11));  // open: gt, lt
  Comparator #(.width(6)) comparator_38 (.a(in_1[31:26]), .b(6'b000001), .eq(out_17));  // open: gt, lt
  Comparator #(.width(6)) comparator_39 (.a(in_1[31:26]), .b(6'b000010), .eq(out_22));  // open: gt, lt

  assign Const = in_1[15:0];
  assign DestJump = in_1[25:0];
  assign Rd = in_1[15:11];
  assign Rs = in_1[25:21];
  assign Rt = in_1[20:16];

  // Other names for the same wires on the sheet: add = out_7; addi = out_36; and = out_8; andi = out_10; beq = out_37;
  //   bgtz = out_11; blez = out_6; bltz = out_17; bne = out_42; div = out_24; divu = out_34; halt = out_15;
  //   FCode[5:0] = in_1[5:0]; X[4:0] = in_1[10:6]; OCode[5:0] = in_1[31:26]; j = out_22; jr = out_40; kbd = out_31;
  //   lw = out_27; mfhi = out_4; mflo = out_9; mult = out_18; mulu = out_29; nop = out_2; nor = out_19; or = out_14;
  //   ori = out_16; pop = out_30; push = out_35; rnd = out_26; slt = out_39; slti = out_41; sltiu = out_5;
  //   sltu = out_3; sub = out_13; sw = out_32; tty = out_20; xor = out_25; xori = out_21
endmodule

module Branch_Control (
  input  in_1,
  input  in_2,
  input  [31:0] in_3,
  input  in_4,
  input  in_5,
  input  in_6,
  input  in_7,
  input  in_8,
  input  [31:0] in_9,
  input  [15:0] in_10,
  input  [25:0] in_11,
  input  [31:0] in_12,
  output [31:0] Output
);

  wire and_1_out, and_2_out, and_3_out, and_4_out, and_5_out, comparator_2_eq, Rs_0, Rs__0, Rs_Rt;
  wire [1:0] SetOp;
  wire [31:0] PC_4, PC_4_OffSet;
  wire [31:18] OffSet_4;

  Comparator #(.width(32)) comparator_1 (.a(in_3), .b(in_9), .eq(Rs_Rt));  // open: gt, lt
  and and_1 (and_1_out, in_1, Rs_Rt);
  and and_2 (and_2_out, ~Rs_Rt, in_4);  // AND_Gate
  and and_3 (and_3_out, in_6, Rs__0);
  and and_4 (and_4_out, in_2, Rs_0);
  and and_5 (and_5_out, ~Rs_0, in_8);  // AND_Gate
  assign OffSet_4 = {{13{1'b0}}, in_10[15]};  // Bit_Extender bit_extender_1
  Comparator #(.width(32)) comparator_2 (.a(in_3), .b({32{1'b0}}), .eq(comparator_2_eq), .lt(Rs_0));  // open: gt
  or or_1 (SetOp[0], and_1_out, and_2_out, and_3_out, and_4_out, and_5_out, in_7);
  or or_2 (SetOp[1], in_5, in_7);
  or or_3 (Rs__0, comparator_2_eq, Rs_0);
  Adder #(.width(32)) adder_1 (.a(in_12), .b(32'h4), .out(PC_4));  // open: cin, cout
  Multiplexer #(.select(2), .width(32), .enable("false")) multiplexer_1 (
    .in0(PC_4), .in1(PC_4_OffSet), .in2({in_12[31:28], in_11, 2'b00}), .out(Output), .sel(SetOp));  // open: in3
  Adder #(.width(32)) adder_2 (.a(PC_4), .b({OffSet_4, in_10, 2'b00}), .out(PC_4_OffSet));  // open: cin, cout

  // Other names for the same wires on the sheet: beq = in_1; bgtz = in_8; blez = in_6; bltz = in_2; bne = in_4;
  //   j = in_5; jr = in_7; DestJump[25:0] = in_11; Jump[31:2] = {in_12[31:28], in_11}; PC[31:0] = in_12;
  //   OffSet[15:0] = in_10; OffSet_4[17:2] = in_10; Rs[31:0] = in_3; Rt[31:0] = in_9
endmodule

module I_O (
  input  [31:0] in_1,
  output [31:0] Output
);


  assign Output = {in_1[7:0], in_1[15:8], in_1[23:16], in_1[31:24]};
endmodule

module Timer (
  input  in_1,
  input  in_2,
  input  in_3,
  input  [3:0] in_4,
  output Output
);

  wire [3:0] counter_1_q;

  Counter #(.width(4), .max('hf)) counter_1 (
    .count(in_3), .Q(counter_1_q), .clk(in_1), .clr(in_2));  // open: load, D, carry
  Comparator #(.width(4)) comparator_1 (.a(in_4), .b(counter_1_q), .eq(Output));  // open: gt, lt

  // Other names for the same wires on the sheet: clk = in_1; reset = in_2; Start = in_3; Time[3:0] = in_4
endmodule

module Instruction (
  input  in_1,
  input  in_2,
  input  in_3,
  input  [31:0] in_4,
  output [31:0] Output
);

  Register #(.width(32)) register_1 (
    .D(in_4), .en(in_3), .Q({Output[7:0], Output[15:8], Output[23:16], Output[31:24]}), .clk(in_1), .clr(in_2));

  // Other names for the same wires on the sheet: clk = in_1; EN = in_3; Instruction[31:0] = in_4; reset = in_2
endmodule

// MA
module Memory_Address (
  input  in_1,
  input  [31:0] in_2,
  input  in_3,
  input  in_4,
  input  in_5,
  input  [31:0] in_6,
  input  in_7,
  input  [31:0] in_8,
  output [31:0] Output
);

  wire [1:0] SelectOut;
  wire [31:0] multiplexer_1_out, subtractor_1_out;

  or or_1 (SelectOut[0], in_1, in_3, in_7);
  or or_2 (SelectOut[1], in_4, in_5, in_7);
  Subtractor #(.width(32)) subtractor_1 (.a(in_8), .b(32'h4), .out(subtractor_1_out));  // open: bin, bout
  Multiplexer #(.width(32), .enable("false")) multiplexer_1 (
    .in0(in_8), .in1(subtractor_1_out), .out(multiplexer_1_out), .sel(in_3));
  Multiplexer #(.select(2), .width(32), .enable("false")) multiplexer_2 (
    .in0(in_6), .in1(multiplexer_1_out), .in2(in_2), .in3(in_6), .out(Output), .sel(SelectOut));

  // Other names for the same wires on the sheet: ALUResult[31:0] = in_2; LW = in_4; PC[31:0] = in_6; PCOut = in_7;
  //   Pop = in_1; Push = in_3; SP[31:0] = in_8; SW = in_5
endmodule

module Operation_Select (
  input  in_1,
  input  in_2,
  input  in_3,
  input  in_4,
  input  in_5,
  input  in_6,
  input  in_7,
  input  in_8,
  input  in_9,
  input  in_10,
  input  in_11,
  input  in_12,
  input  in_13,
  input  in_14,
  input  in_15,
  input  in_16,
  input  in_17,
  input  in_18,
  output ALU_ON,
  output No_Sign,
  output Inmediate,
  output [3:0] Selector
);

  wire Add_Addi, AllSlt, And_Andi, Mult_Mulu, Or_Ori, Xor_Xori;

  or or_1 (Add_Addi, in_1, in_4);
  or or_2 (And_Andi, in_5, in_18);
  or or_3 (Or_Ori, in_8, in_3);
  or or_4 (Xor_Xori, in_12, in_6);
  or or_5 (Mult_Mulu, in_9, in_13);
  or or_6 (Selector[3], in_11, in_15);
  or or_7 (AllSlt, in_17, in_2, in_14, in_16);
  or or_8 (No_Sign, in_13, in_2, in_15, in_16);
  or or_9 (Selector[0], Add_Addi, And_Andi, Selector[3], Xor_Xori, AllSlt);
  or or_10 (Selector[1], in_7, And_Andi, in_10, Selector[3], AllSlt);
  or or_11 (Selector[2], Or_Ori, in_10, Xor_Xori, AllSlt, Selector[3]);
  or or_12 (Inmediate, in_1, in_18, in_3, in_6, in_14);
  or or_13 (ALU_ON, Selector[0], Selector[1], Selector[2], Selector[3], Mult_Mulu);

  // Other names for the same wires on the sheet: add = in_4; addi = in_1; and = in_5; andi = in_18; div = in_11;
  //   divu = in_15; mult = in_9; mulu = in_13; nor = in_10; or = in_8; ori = in_3; _1 = Selector[0]; _2 = Selector[1];
  //   _3 = Selector[2]; Div_Divu = Selector[3]; slt = in_17; slti = in_14; sltiu = in_16; sltu = in_2; sub = in_7;
  //   xor = in_12; xori = in_6
endmodule

module Data_Path (
  input  [31:0] in_1,
  input  in_2,
  input  in_3,
  input  in_4,
  input  in_5,
  input  in_6,
  input  in_7,
  input  in_8,
  input  [6:0] in_9,
  output Write,
  output ALUI,
  output Stack,
  output Memory,
  output Tty,
  output Jump,
  output RI,
  output Halt,
  output [31:0] Address,
  output [6:0] TtyData,
  output [31:0] ROut
);

  wire Add, Addi, AddiO, ALUOn, And, Andi, Beq, Bgtz, Blez, Bltz, Bne, Div, Divu, Inmediate, J, Jr, Kbd, LW,
       Mfhi, Mflo, Mult, Mulu, No_Andi_Xori_Ori, Nop, Nor, NoSign, Or, Ori, Pop, Push, Rnd, Slt, Slti, Sltiu,
       Sltu, Sub, SW, Xor, Xori;
  wire [2:0] SelectRF;
  wire [3:0] SelectALU;
  wire [4:0] Dest, Rd, Rs_t, Rt_t;
  wire [15:0] Const;
  wire [25:0] DestJump;
  wire [31:0] ALUR, ALUResult, branch_control_1_output, HI, instruction_1_output, KeyBInput32, LO, PC,
       Random, RFInput, Rt, Rt_Const, SP;
  wire [31:7] Rs;
  wire [31:31] and_2_out;

  Instruction instruction_1 (.in_1(in_2), .in_2(in_5), .in_3(in_8), .in_4(in_1), .Output(instruction_1_output));
  Multiplexer #(.width(5), .enable("false")) multiplexer_1 (.in0(Rd), .in1(Rt_t), .out(Dest), .sel(Inmediate));
  assign KeyBInput32 = {{25{1'b0}}, in_9};  // Bit_Extender bit_extender_1
  Random #(.width(32)) random_1 (.clk(in_2), .next(Rnd), .out(Random));  // open: clr
  Register_File register_file_1 (
    .in_1(in_2), .in_2(Push), .in_3(RFInput), .in_4(in_5), .in_5(in_6), .in_6(in_7), .in_7(Pop),
    .Destination(Dest), .in_9(Rs_t), .in_10(Rt_t), .Stack_Pointer(SP), .Output_A({Rs, TtyData}), .Output_B(Rt));
  or or_1 (AddiO, SW, LW, Addi);
  and and_1 (No_Andi_Xori_Ori, ~Xori, ~Andi, ~Ori);  // AND_Gate
  or or_2 (ALUI, Mulu, Add, Or, Addi, Div, And, Ori, Andi, Xor, Mult, Divu, Sub, Nor, Sltiu, Xori, Slti, Sltu, Slt);
  or or_3 (Jump, Bne, Nop, Beq, Bgtz, J, Bltz, Jr, Blez);
  Instruction_Decoder instruction_decoder_1 (
    .out_2(Nop), .out_3(Sltu), .out_4(Mfhi), .out_5(Sltiu), .out_6(Blez), .out_7(Add), .out_8(And),
    .out_9(Mflo), .out_10(Andi), .out_11(Bgtz), .DestJump(DestJump), .in_1(instruction_1_output),
    .out_13(Sub), .out_14(Or), .out_15(Halt), .out_16(Ori), .out_17(Bltz), .out_18(Mult), .out_19(Nor),
    .out_20(Tty), .out_21(Xori), .out_22(J), .Const(Const), .out_24(Div), .out_25(Xor), .out_26(Rnd),
    .out_27(LW), .Rs(Rs_t), .out_29(Mulu), .out_30(Pop), .out_31(Kbd), .out_32(SW), .Rt(Rt_t), .out_34(Divu),
    .out_35(Push), .out_36(Addi), .out_37(Beq), .Rd(Rd), .out_39(Slt), .out_40(Jr), .out_41(Slti),
    .out_42(Bne));
  Operation_Select operation_select_1 (
    .in_1(Addi), .in_2(Sltu), .in_3(Ori), .in_4(Add), .in_5(And), .in_6(Xori), .in_7(Sub), .in_8(Or),
    .in_9(Mult), .in_10(Nor), .in_11(Div), .in_12(Xor), .in_13(Mulu), .in_14(Slti), .in_15(Divu),
    .in_16(Sltiu), .in_17(Slt), .in_18(Andi), .ALU_ON(ALUOn), .No_Sign(NoSign), .Inmediate(Inmediate),
    .Selector(SelectALU));
  and and_2 (and_2_out[31], No_Andi_Xori_Ori, Const[15]);
  Multiplexer #(.width(32), .enable("false")) multiplexer_2 (
    .in0(Rt), .in1({{16{and_2_out[31]}}, Const}), .out(Rt_Const), .sel(Inmediate));
  or or_4 (Write, Push, SW);
  or or_5 (Stack, Pop, Push);
  or or_6 (Memory, SW, LW);
  or or_7 (RI, Mflo, Tty, Rnd, Mfhi, Kbd);
  ALU alu_1 (
    .in_1(in_2), .A({Rs, TtyData}), .in_3(ALUOn), .B(Rt_Const), .in_5(NoSign), .in_6(SelectALU), .Output(LO),
    .Output_2(ALUR), .Output_3(HI));
  or or_8 (SelectRF[0], LW, Pop, Mflo, Kbd);
  or or_9 (SelectRF[1], Mflo, Mfhi);
  or or_10 (SelectRF[2], Kbd, Rnd);
  Memory_Address memory_address_1 (
    .in_1(Pop), .in_2(ALUResult), .in_3(Push), .in_4(LW), .in_5(SW), .in_6(PC), .in_7(in_4), .in_8(SP),
    .Output(Address));
  Multiplexer #(.width(32), .enable("false")) multiplexer_3 (.in0({Rs, TtyData}), .in1(Rt), .out(ROut), .sel(SW));
  Branch_Control branch_control_1 (
    .in_1(Beq), .in_2(Bltz), .in_3({Rs, TtyData}), .in_4(Bne), .in_5(J), .in_6(Blez), .in_7(Jr), .in_8(Bgtz),
    .in_9(Rt), .in_10(Const), .in_11(DestJump), .in_12(PC), .Output(branch_control_1_output));
  Multiplexer #(.select(3), .width(32), .enable("false")) multiplexer_4 (
    .in0(ALUR), .in1(LO), .in2(HI), .in3(in_1), .in4(KeyBInput32), .in5(Random), .out(RFInput), .sel(SelectRF));  // open: in6, in7
  Program_Counter program_counter_1 (
    .in_1(branch_control_1_output), .in_4(in_6), .Output(PC), .in_2(in_2), .in_3(in_5));

  // Other names for the same wires on the sheet: Clk = in_2; EnableGI = in_8; EnablePC = in_6; EnableRF = in_7;
  //   Instruction[31:0] = in_1; KeyBAva = in_3; KeyBInput[6:0] = in_9; NextOK = in_4; Reset = in_5; Rs[6:0] = TtyData
endmodule

module Read_Ram (
  input  [15:0] ADDR,
  input  [31:0] Bank_0,
  input  [31:0] Bank_1,
  input  [31:0] Bank_2,
  input  [31:0] Bank_3,
  input  [3:0] in_6,
  input  in_7,
  input  in_8,
  input  in_9,
  input  in_10,
  output [31:0] BankOut_0,
  output [31:0] BankOut_1,
  output [31:0] BankOut_2,
  output [31:0] BankOut_3,
  output Ready,
  output CS
);

  wire A, and_3_out, and_4_out, comparator_1_eq, Cont, d_ff_4_q, GetRead, multiplexer_1_out, or_1_out,
       ReadyRead, ResetMem, RM, Stop, X;
  wire [15:0] ADDRMem;

  and and_1 (GetRead, in_9, ~Cont);  // AND_Gate
  Comparator #(.width(16)) comparator_1 (.a(ADDR), .b(ADDRMem), .eq(comparator_1_eq));  // open: gt, lt
  D_Flip_Flop #(.trigger("falling")) d_ff_1 (.clk(in_7), .D(GetRead), .Q(A), .en(or_1_out));  // open: Qn, preset, reset
  or or_1 (or_1_out, GetRead, Stop);
  and and_2 (Cont, ~ResetMem, comparator_1_eq);  // AND_Gate
  Timer timer_1 (.in_1(in_7), .in_2(ReadyRead), .in_3(A), .in_4(in_6), .Output(Stop));
  or or_2 (CS, X, A);
  and and_3 (and_3_out, Cont, in_10);
  D_Flip_Flop #(.trigger("falling")) d_ff_2 (.clk(in_7), .D(Stop), .Q(X), .reset(ReadyRead));  // open: Qn, preset, en
  or or_3 (RM, and_3_out, in_8);
  D_Flip_Flop #(.trigger("falling")) d_ff_3 (.clk(in_7), .D(X), .Q(ReadyRead));  // open: Qn, preset, en, reset
  Multiplexer #(.enable("false")) multiplexer_1 (.in0(ResetMem), .in1(RM), .out(multiplexer_1_out), .sel(RM));
  D_Flip_Flop #(.trigger("falling")) d_ff_4 (
    .clk(in_7), .D(and_4_out), .Q(d_ff_4_q), .reset(in_8));  // open: Qn, preset, en
  and and_4 (and_4_out, in_9, Cont);
  D_Flip_Flop #(.trigger("falling")) d_ff_5 (
    .clk(in_7), .D(multiplexer_1_out), .Q(ResetMem), .reset(ReadyRead));  // open: Qn, preset, en
  Register #(.width(32)) register_1 (.D(Bank_0), .en(X), .Q(BankOut_0), .clk(in_7), .clr(in_8));
  Register #(.width(32)) register_2 (.D(Bank_1), .en(X), .Q(BankOut_1), .clk(in_7), .clr(in_8));
  Register #(.width(16)) register_3 (.D(ADDR), .en(X), .Q(ADDRMem), .clk(in_7), .clr(in_8));
  or or_4 (Ready, ReadyRead, d_ff_4_q);
  Register #(.width(32)) register_4 (.D(Bank_2), .en(X), .Q(BankOut_2), .clk(in_7), .clr(in_8));
  Register #(.width(32)) register_5 (.D(Bank_3), .en(X), .Q(BankOut_3), .clk(in_7), .clr(in_8));

  // Other names for the same wires on the sheet: Clk = in_7; Get = in_9; ReadTime[3:0] = in_6; Reset = in_8;
  //   Write = in_10
endmodule

// RI
module RamI (
  input  [31:0] Bank_0,
  input  [31:0] Bank_1,
  input  [31:0] Bank_2,
  input  [31:0] Bank_3,
  input  [31:0] DPAddress,
  input  [3:0] in_6,
  input  in_7,
  input  in_8,
  input  in_9,
  input  in_10,
  input  in_11,
  input  in_12,
  input  [3:0] WriteTime,
  output [3:0] Mask,
  output [15:0] ADDR,
  output [31:0] BankOut_0,
  output [31:0] BankOut_1,
  output [31:0] BankOut_2,
  output [31:0] BankOut_3,
  output Ready,
  output CS,
  output RW,
  output ReadyData,
  output ReadyWrite
);

  wire CSD, CSl, or_1_out, Stop0;
  wire [31:0] DO0, DO1, DO2, DO3, i_o_1_output, i_o_2_output, i_o_3_output, i_o_4_output, IO0, IO1, IO2, IO3;

  D_Flip_Flop #(.trigger("falling")) d_ff_1 (.clk(in_7), .D(in_10), .Q(RW), .en(or_1_out));  // open: Qn, preset, reset
  or or_1 (or_1_out, in_10, Stop0);
  Read_Ram read_ram_1 (
    .ADDR(DPAddress[19:4]), .Bank_0(Bank_0), .Bank_1(Bank_1), .Bank_2(Bank_2), .Bank_3(Bank_3), .in_6(in_6),
    .in_7(in_7), .in_8(in_8), .in_9(in_9), .in_10(in_10), .BankOut_0(IO0), .BankOut_1(IO1), .BankOut_2(IO2),
    .BankOut_3(IO3), .Ready(Ready), .CS(CSl));
  Timer timer_1 (.in_1(in_7), .in_2(ReadyWrite), .in_3(RW), .in_4(WriteTime), .Output(Stop0));
  D_Flip_Flop #(.trigger("falling")) d_ff_2 (.clk(in_7), .D(Stop0), .Q(ReadyWrite));  // open: Qn, preset, en, reset
  Read_Ram read_ram_2 (
    .ADDR(DPAddress[19:4]), .Bank_0(Bank_0), .Bank_1(Bank_1), .Bank_2(Bank_2), .Bank_3(Bank_3), .in_6(in_6),
    .in_7(in_7), .in_8(in_8), .in_9(in_11), .in_10(in_10), .BankOut_0(DO0), .BankOut_1(DO1), .BankOut_2(DO2),
    .BankOut_3(DO3), .Ready(ReadyData), .CS(CSD));
  or or_2 (CS, RW, CSl, CSD);
  Demultiplexer #(.select(2), .enable("false")) demultiplexer_1 (
    .out0(Mask[0]), .out1(Mask[1]), .out2(Mask[2]), .out3(Mask[3]), .in(1'b1), .sel(DPAddress[3:2]));
  I_O i_o_1 (.in_1(DO0), .Output(i_o_1_output));
  I_O i_o_2 (.in_1(DO1), .Output(i_o_2_output));
  I_O i_o_3 (.in_1(DO2), .Output(i_o_3_output));
  I_O i_o_4 (.in_1(DO3), .Output(i_o_4_output));
  Multiplexer #(.width(32), .enable("false")) multiplexer_1 (
    .in0(i_o_1_output), .in1(IO0), .out(BankOut_0), .sel(in_12));
  Multiplexer #(.width(32), .enable("false")) multiplexer_2 (
    .in0(i_o_2_output), .in1(IO1), .out(BankOut_1), .sel(in_12));
  Multiplexer #(.width(32), .enable("false")) multiplexer_3 (
    .in0(i_o_3_output), .in1(IO2), .out(BankOut_2), .sel(in_12));
  Multiplexer #(.width(32), .enable("false")) multiplexer_4 (
    .in0(i_o_4_output), .in1(IO3), .out(BankOut_3), .sel(in_12));

  assign ADDR = DPAddress[19:4];

  // Other names for the same wires on the sheet: Clk = in_7; Get = in_9; GetData = in_11; lsl = in_12;
  //   ReadTime[3:0] = in_6; Reset = in_8; Write = in_10
endmodule

// CU
module Control_Unit (
  input  Clk,
  input  ReadyData,
  input  Reset,
  input  ReadyI,
  input  Start,
  input  ReadyW,
  input  MemoryI,
  input  RI,
  input  Altul,
  input  JumpI,
  input  WriteI,
  input  Ttyl,
  output GetI,
  output Write,
  output GetData,
  output End,
  output UseRF,
  output UseGI,
  output TtyEn,
  output KeyboardEn,
  output UsePC
);

  wire Branch, d_ff_1_q, d_ff_3_q, d_ff_4_q, d_ff_5_q, demultiplexer_1_out0, demultiplexer_1_out1, or_4_out,
       RF;
  wire [2:0] SelectOut;

  D_Flip_Flop #(.trigger("falling")) d_ff_1 (
    .clk(Clk), .D(ReadyI), .Q(d_ff_1_q), .reset(Reset));  // open: Qn, preset, en
  or or_1 (SelectOut[0], Altul, WriteI, RI);
  or or_2 (SelectOut[1], RI, JumpI);
  or or_3 (SelectOut[2], MemoryI, WriteI);
  Demultiplexer #(.select(3)) demultiplexer_1 (
    .out0(demultiplexer_1_out0), .out1(demultiplexer_1_out1), .out2(Branch), .out3(RF), .out4(GetData),
    .out5(Write), .in(d_ff_1_q), .sel(SelectOut));  // open: out6, out7, en
  or or_4 (or_4_out, End, demultiplexer_1_out0);
  D_Flip_Flop #(.trigger("falling")) d_ff_2 (.clk(Clk), .D(or_4_out), .Q(End), .reset(Reset));  // open: Qn, preset, en
  D_Flip_Flop #(.trigger("falling")) d_ff_3 (
    .clk(Clk), .D(demultiplexer_1_out1), .Q(d_ff_3_q), .reset(Reset));  // open: Qn, preset, en
  D_Flip_Flop #(.trigger("falling")) d_ff_4 (
    .clk(Clk), .D(Start), .Q(d_ff_4_q), .reset(Reset));  // open: Qn, preset, en
  D_Flip_Flop #(.trigger("falling")) d_ff_5 (
    .clk(Clk), .D(UsePC), .Q(d_ff_5_q), .reset(Reset));  // open: Qn, preset, en
  or or_5 (UseRF, d_ff_3_q, ReadyData, RF);
  or or_6 (GetI, d_ff_4_q, d_ff_5_q);
  D_Flip_Flop #(.trigger("falling")) d_ff_6 (.clk(Clk), .D(UseRF), .Q(KeyboardEn));  // open: Qn, preset, en, reset
  and and_1 (TtyEn, Ttyl, KeyboardEn);
  or or_7 (UsePC, KeyboardEn, ReadyW, Branch);

  assign UseGI = ReadyI;

  // Other names for the same wires on the sheet: Cont = UsePC; Tty = KeyboardEn
endmodule
